# Fritzing sketch Cosma_Sensor_Board_01 (saved by Fritzing 0.9.3b)
circuit board: 6.70584cm x 4.75019cm

parts:
  Arduino = Arduino Pro Mini v13
  Connector_to_Sensor_Board = M16 [package=1x16_machine-pin-header_lock.004]
  Part1 = Triple Axis Accelerometer Breakout - ADXL345
  Edge_Connector = M16 [package=1x16_machine-pin-header_lock.004]

nets:
  VCC: Arduino.VCC, Part1.VCC
  GND: Arduino.GND, Connector_to_Sensor_Board.3_-_Gray, Part1.GND
  N1: Arduino.A4, Part1.SDA
  N2: Arduino.A5, Part1.SCL
  N3: Arduino.RAW, Connector_to_Sensor_Board.6_-_Green, Edge_Connector.10, Edge_Connector.11
  N4: Arduino.D13/SCK, Edge_Connector.16
  N5: Arduino.D12/MISO, Edge_Connector.15
  N6: Arduino.D11_PWM/MOSI, Edge_Connector.14
  N7: Arduino.D10_PWM/SS, Edge_Connector.13
  N8: Arduino.D8, Connector_to_Sensor_Board.9_-_Red
  N9: Arduino.D7, Connector_to_Sensor_Board.2_-_White
  N10: Arduino.D6_PWM, Connector_to_Sensor_Board.1_-_Black
  N11: Arduino.D5_PWM, Connector_to_Sensor_Board.4_-_Purple
  N12: Arduino.D3_PWM, Connector_to_Sensor_Board.10_-_Brown
  N13: Arduino.D2, Connector_to_Sensor_Board.5_-_Blue

custom parts:
  M16: 1x16 .1 header
